// Logisim project tp4_cpt4.circ as structural Verilog: 1 circuit, main circuit cpt4
module cpt4 (
  output [3:0] out_1
);

  wire clock_1_out;
  wire [3:0] adder_1_out;

  Clock clock_1 (.out(clock_1_out));
  D_Flip_Flop d_ff_1 (.clk(clock_1_out), .D(adder_1_out[3]), .Q(out_1[3]));  // open: Qn, preset, en, reset
  D_Flip_Flop d_ff_2 (.clk(clock_1_out), .D(adder_1_out[2]), .Q(out_1[2]));  // open: Qn, preset, en, reset
  D_Flip_Flop d_ff_3 (.clk(clock_1_out), .D(adder_1_out[1]), .Q(out_1[1]));  // open: Qn, preset, en, reset
  D_Flip_Flop d_ff_4 (.clk(clock_1_out), .D(adder_1_out[0]), .Q(out_1[0]));  // open: Qn, preset, en, reset
  Adder #(.width(4)) adder_1 (.a(4'b0000), .b(out_1), .out(adder_1_out), .cin(1'b1));  // open: cout

  // Notes on the sheet:
  //   valeur courante
  //   Compteur 4 bits
endmodule
