// Logisim project tp4_test_add4.circ as structural Verilog: 3 circuits, main circuit main
module main (
  output [7:0] out_1,
  output halt,
  output [4:0] out_3,
  output same
);

  wire clock_1_out, comparator_1_eq, not_1_out;

  Clock clock_1 (.out(clock_1_out));
  Counter counter_1 (.Q(out_1), .clk(clock_1_out));  // open: load, D, count, carry, clr
  Adder #(.width(4)) adder_1 (.a(out_1[7:4]), .b(out_1[3:0]), .out(out_3[3:0]), .cin(1'b0), .cout(out_3[4]));
  Comparator #(.mode("unsigned")) comparator_1 (.a(out_1), .b({8{1'b1}}), .eq(comparator_1_eq));  // open: gt, lt
  not not_1 (not_1_out, same);
  Comparator #(.width(5), .mode("unsigned")) comparator_2 (.a(out_3), .b({5{1'b1}}), .eq(same));  // open: gt, lt
  or or_1 (halt, comparator_1_eq, not_1_out);
endmodule

module FA (
  input  b,
  input  a,
  input  ci,
  output co,
  output s
);

  wire or_1_out, or_2_out, xor_2_out;

  xor xor_1 (co, or_1_out, or_2_out);
  or or_1 (or_1_out, a, b);
  or or_2 (or_2_out, xor_2_out, ci);
  xor xor_2 (xor_2_out, b, a);
  xor xor_3 (s, ci, xor_2_out);
endmodule

module add4 (
  input  [3:0] b,
  input  [3:0] a,
  output co,
  output [3:0] s
);

  wire fa_2_co, fa_3_co, fa_4_co;

  FA fa_1 (.b(b[3]), .a(a[3]), .s(co), .ci(fa_2_co));  // open: co
  FA fa_2 (.co(fa_2_co), .b(b[2]), .a(a[2]), .s(s[2]), .ci(fa_3_co));
  FA fa_3 (.co(fa_3_co), .b(b[1]), .a(a[1]), .s(s[1]), .ci(fa_4_co));
  FA fa_4 (.co(fa_4_co), .b(b[0]), .a(a[0]), .s(s[0]), .ci(1'b0));

  assign s[3] = co;
endmodule
